# Fritzing sketch Jonas (saved by Fritzing 0.9.3b)
breadboards: 1

parts:
  R1 = Rotary Potentiometer (Small) [maximum_resistance=100kΩ package=THT]
  Part1 = Arduino Uno (Rev3)
  M1 = DC Motor
  IC1 = L293D [package=THT]
  LCD1 = LCD screen  # not connected
  VCC1 = Battery block 9V
  LCM1602_IIC1 = LCM1602 IIC [part_number="LCM1602 IIC" chip_label="LCM1602 IIC" package="DIP (Dual Inline) [THT]"]
  LM1 = Capteur IR CAP227 - 3 pins [package=THT]

nets:
  5V: R1.leg1, Part1.5V, IC1.Enable_1, IC1.+V, LCM1602_IIC1.VCC, LM1.pin3
  N1: R1.wiper, Part1.A0
  GND: R1.leg2, Part1.GND, M1.pin_2, IC1.0V, VCC1.-, LCM1602_IIC1.GND, LM1.pin1
  N2: Part1.A4/SDA, LCM1602_IIC1.SDA
  N3: Part1.A5/SCL, LCM1602_IIC1.SCL
  N4: Part1.D5_PWM, LM1.pin2
  N5: Part1.D6_PWM, IC1.In_1
  N6: M1.pin_1, IC1.Out_1_(_Controlled_by_Enable_1_)
  N7: IC1.+Vmotor, VCC1.+

notes:
  9V GND verbinden für Common Ground. Sonst fließt evtl. Motorstrom durch Arduino. Letzterer dann putt.
  Eigene Stromquelle an Arduino anschließen.
  Digitalen Sensorausgang benutzen.
  (Du hast 4, hier nur 3)
  "LM393" bezeichnet nur den Comparator, nicht die Sensorart selbst.

custom parts:
  LCM1602 IIC: I2C-Module to use a 1602 or 2004 LCD on with the wire.h libory Serial LCD Modul
  Capteur IR CAP227 - 3 pins: Capteur IR pour suiveur de ligne CAP227 A base de LM 393 Créateur : Gaetan Brissot Fournisseur : centralmedia.fr

// code stored in the sketch: Jonas.ino
#include <Wire.h>
/* !! ACHTUNG !!
 * Unbedingt "LiquidCrystal I2C" von <Frank de Brabander>
 * via Arduino Library Manager installieren.
 */
#include <LiquidCrystal_I2C.h>

/* PINS:
 * 
 * - A0: Potentiometer für Motorsteuerung (0V-5V)
 * - A4: Display SDA (Datensignal für Display. I2C-Bus)
 * - A5: Display SCL (Clocksignal für Display. I2C-Bus)
 * - ~5: Speed Sensor digitaler Ausgang (LOW: dunkel, HIGH: hell. Wir zählen die Sprünge
 *                                       LOW->HIGH und machen eine Drehzahl draus)
 * - ~6: H-Brücke, Pin 2 (Steuersignal für Motor 1, PWM. 0-255 = 0V-5V)
 */

const int PIN_POTI = A0;
// LCD Pins werden über LiquidCrystal_I2C-Bibliothek gesetzt.
const int PIN_MOTOR = 5;
const int PIN_SENSOR = 6;

const int SPEED_SENSOR_SEGMENTS = 20;
const int BEATS_PRO_UMDREHUNG = 1;

/** Display in lcd-Variable einrichten. Initialisierung findet später statt.
 * 0x27: I2C-Adresse des Displays
 * 16: 16 Spalten
 * 2: 2 Zeilen
 */
LiquidCrystal_I2C lcd(0x27, 16, 2);

int bpm_last_millis = 0;
int bpm = 0;
const char BPM_SUFFIX = ""; // z.B. "BPM" oder "u/min". max. 9 Zeichen.


void setup() 
{
  lcd.init(); // Display initialisieren
  lcd.backlight(); // Es werde Licht

  // obere Zeile im Display. Bleibt ja gleich.
  lcd.setCursor(0, 0);
  lcd.print("BPM:");

  pinMode(PIN_POTI, INPUT);
  pinMode(PIN_MOTOR, OUTPUT);

  // Interrupt setzen, um BPM via Sensor zu zählen
  pinMode(PIN_SENSOR, INPUT_PULLUP);
  attachInterrupt(digitalPinToInterrupt(PIN_SENSOR), bpmInterrupt, RISING);
}

/**
 * Diese Funktion wird per Interrupt aufgerufen, sobald der Sensor Licht sieht.
 */
void bpmInterrupt() {
  int bpm_diff_millis = bpm_last_millis - millis();
  bpm_last_millis = millis();

  const int millis_per_minute = 60000;

  bpm = millis_per_minute / (bpm_diff_millis * SPEED_SENSOR_SEGMENTS)
}

/**
 * Gibt BPM schön formatiert auf Display aus
 */
void writeDisplay() {
  lcd.setCursor(0, 1);
  char buffer[16];
  sprintf(buffer, "%6d%-9s", bpm, BPM_SUFFIX); // fügt bpm und BPM_SUFFIX zu einer Zeile zusammen
  lcd.print(buffer);
}

void controlMotor() {
  int poti = analogRead(PIN_POTI); // von 0 bis 1023
  int motor = map(poti, 0, 1023, 0, 255) // Reskalierung auf 0 bis 255
	analogWrite(PIN_MOTOR, motor);
}

/** Arduino Hauptschleife
 * Aufgaben:
 *  1. Poti lesen und direkt an Motor übergeben. Nix speichern.
 *  2. BPM auf Display ausgeben.
 *
 *  BPM werden vom Sensor per Interrupt ermittelt. Ist einfacher.
 */
void loop() 
{
  controlMotor();
  writeDisplay();
}
